// Logisim project fizz.circ as structural Verilog: 5 circuits, main circuit main
module main (
  input  master_clock
);

  wire and_1_out, clock_1_out, control_1_bneq, control_1_branch, control_1_jump, control_1_memread,
       control_1_memtoreg, control_1_memwrite, control_1_regdest, control_1_regwrite, mips_alu_1_p4,
       xor_1_out;
  wire [1:0] control_1_alusrc;
  wire [3:0] instruction_decode_1_dstreg, instruction_decode_1_opcode, instruction_decode_1_shiftamount,
       instruction_decode_1_srcreg1, instruction_decode_1_srcreg2, multiplexer_1_out, rom_2_data;
  wire [7:0] adder_1_out, adder_2_out, bit_extender_2_out, bit_extender_4_out,
       instruction_decode_1_address_imm, instruction_decode_1_targetjump, multiplexer_2_out,
       multiplexer_3_out, multiplexer_4_out, multiplexer_5_out, ram_1_data, register_1_q,
       registers_1_data_out_a, registers_1_data_out_b, undriven;
  wire [19:0] rom_1_data;
  wire [31:0] bit_extender_1_out, bit_extender_3_out, mips_alu_1_p5;

  Clock clock_1 (.out(clock_1_out));
  Register register_1 (.D(multiplexer_5_out), .Q(register_1_q), .clk(clock_1_out));  // open: en, clr
  Adder adder_1 (.a(8'h1), .b(register_1_q), .out(adder_1_out));  // open: cin, cout
  Multiplexer #(.width(4), .enable("false")) multiplexer_1 (
    .in0(instruction_decode_1_srcreg2), .in1(instruction_decode_1_dstreg), .out(multiplexer_1_out),
    .sel(control_1_regdest));
  ROM #(.dataWidth(20)) rom_1 (.addr(register_1_q), .data(rom_1_data));  // open: sel
  Instruction_Decode instruction_decode_1 (
    .in_1(rom_1_data), .shiftAmount(instruction_decode_1_shiftamount), .DstReg(instruction_decode_1_dstreg),
    .Address_Imm(instruction_decode_1_address_imm), .SrcReg2(instruction_decode_1_srcreg2),
    .SrcReg1(instruction_decode_1_srcreg1), .TargetJump(instruction_decode_1_targetjump),
    .opCode(instruction_decode_1_opcode));
  Registers registers_1 (
    .clock(clock_1_out), .data_in(multiplexer_4_out), .regWrite(control_1_regwrite),
    .addressA(instruction_decode_1_srcreg1), .addressB__ReadOnly(instruction_decode_1_srcreg2),
    .data_out_A(registers_1_data_out_a), .data_out_B(registers_1_data_out_b), .write(multiplexer_1_out));
  assign bit_extender_1_out = {{24{registers_1_data_out_a[7]}}, registers_1_data_out_a};  // Bit_Extender bit_extender_1
  Multiplexer #(.select(2), .width(8), .enable("false")) multiplexer_2 (
    .in0(registers_1_data_out_b), .in1(instruction_decode_1_address_imm), .in2(bit_extender_2_out),
    .in3(bit_extender_2_out), .out(multiplexer_2_out), .sel(control_1_alusrc));
  assign bit_extender_2_out = {{4{instruction_decode_1_shiftamount[3]}}, instruction_decode_1_shiftamount};  // Bit_Extender bit_extender_2
  ROM #(.addrWidth(4), .dataWidth(4)) rom_2 (.addr(instruction_decode_1_opcode), .data(rom_2_data));  // open: sel
  assign bit_extender_3_out = {{24{multiplexer_2_out[7]}}, multiplexer_2_out};  // Bit_Extender bit_extender_3
  // MIPS_ALU mips_alu_1: pin names not known; wires that end beside it: bit_extender_1_out, bit_extender_3_out, rom_2_data, mips_alu_1_p4, mips_alu_1_p5
  Control control_1 (
    .in_1(instruction_decode_1_opcode), .bneq(control_1_bneq), .Shift(control_1_alusrc[1]),
    .RegDest(control_1_regdest), .Jump(control_1_jump), .Branch(control_1_branch),
    .MemRead(control_1_memread), .MemToReg(control_1_memtoreg), .MemWrite(control_1_memwrite),
    .ALUSrc(control_1_alusrc[0]), .RegWrite(control_1_regwrite));
  Bit_Extender #(.in_width(32), .out_width(8), .\type ("sign")) bit_extender_4 (
    .in(mips_alu_1_p5), .out(bit_extender_4_out));
  Adder adder_2 (.a(adder_1_out), .b(undriven), .out(adder_2_out));  // open: cin, cout
  xor xor_1 (xor_1_out, mips_alu_1_p4, control_1_bneq);
  RAM #(.bus("separate")) ram_1 (
    .addr(bit_extender_4_out), .din(registers_1_data_out_b), .data(ram_1_data), .str(control_1_memwrite),
    .clk(clock_1_out), .ld(control_1_memread));  // open: sel, clr
  Multiplexer #(.width(8), .enable("false")) multiplexer_3 (
    .in0(adder_1_out), .in1(adder_2_out), .out(multiplexer_3_out), .sel(and_1_out));
  and and_1 (and_1_out, xor_1_out, control_1_branch);
  Multiplexer #(.width(8)) multiplexer_4 (
    .in0(bit_extender_4_out), .in1(ram_1_data), .out(multiplexer_4_out), .sel(control_1_memtoreg));  // open: en
  Multiplexer #(.width(8), .enable("false")) multiplexer_5 (
    .in0(multiplexer_3_out), .in1(instruction_decode_1_targetjump), .out(multiplexer_5_out),
    .sel(control_1_jump));

  // Notes on the sheet:
  //   PC
  //   contents of rom_1 (hex, n*v repeats v):
  //   68567 34234 34234 67867 63445 34234 36345 34234 56457 58967 45345 45780 57890 70789 67856 57456
  //   23123 41241 41234 41234 35346 67556 96780 74536 45234 57568 59780 90897 63464 57869 53789 45780
  //   78970 89789 89678 67967 79789 89789 67967 89789 89678 78678 86745 34534 5346 67658 79789 96879 65745
  //   34534 34765 34765 45345 34534 45346 45634 34534 64356 45634 45346 34534 34534 34634 56534 53464
  //   45634 5345 46345 34534 35634 5
  //   opcode
  //   immediate value/address
  //   contents of rom_2 (hex, n*v repeats v):
  //   f 6 6 2 6 2 2 2 1 8 9 6 c 0 1
  //   shamt
  //   if shift
  //   MAKE ALU 8 BIT AGAIN
  //   ALU SRC
  //   branching
  //   branch address
  //   bneq
  //   MEM WRITE
  //   MEM READ
  //   bneq OR beq
  //   JUMP ADDRESS
  //   MEM TO REG
  //   JUMP
endmodule

module Abro_Logical_Unit (
  input  [7:0] in_1,
  input  [7:0] in_2,
  input  [2:0] in_3,
  output [7:0] out_4
);

  wire [7:0] adder_1_out, and_1_out, nor_1_out, or_1_out, subtractor_1_out;

  Adder adder_1 (.a(in_1), .b(in_2), .out(adder_1_out));  // open: cin, cout
  Subtractor subtractor_1 (.a(in_1), .b(in_2), .out(subtractor_1_out));  // open: bin, bout
  assign and_1_out = in_1 & in_2;  // AND_Gate and_1, 8 bits wide
  assign or_1_out = in_1 | in_2;  // OR_Gate or_1, 8 bits wide
  assign nor_1_out = ~(in_1 | in_2);  // NOR_Gate nor_1, 8 bits wide
  Multiplexer #(.select(3), .width(8)) multiplexer_1 (
    .in0(adder_1_out), .in1(subtractor_1_out), .in2(and_1_out), .in3(or_1_out), .in4(nor_1_out), .out(out_4),
    .sel(in_3));  // open: in5, in6, in7, en
endmodule

module Registers (
  input  clock,
  input  [7:0] data_in,
  input  regWrite,
  input  [3:0] write,
  input  [3:0] addressA,
  input  [3:0] addressB__ReadOnly,
  output [7:0] data_out_A,
  output [7:0] data_out_B
);

  wire demultiplexer_1_out0, demultiplexer_1_out1, demultiplexer_1_out2, demultiplexer_1_out3,
       demultiplexer_1_out4, demultiplexer_1_out10, demultiplexer_1_out14;
  wire [7:0] SP_q, t0_q, t1_q, t2_q, t3_q, t4_q, ZERO_q;

  Demultiplexer #(.select(4)) demultiplexer_1 (
    .out0(demultiplexer_1_out0), .out1(demultiplexer_1_out1), .out2(demultiplexer_1_out2),
    .out3(demultiplexer_1_out3), .out4(demultiplexer_1_out4), .out10(demultiplexer_1_out10),
    .out14(demultiplexer_1_out14), .out15(demultiplexer_1_out14), .in(regWrite), .sel(write));  // open: out5, out6, out7, out8, out9, out11, out12, out13, en
  Register #(.trigger("falling")) t0 (.D(data_in), .en(demultiplexer_1_out0), .Q(t0_q), .clk(clock));  // open: clr
  Register #(.trigger("falling")) t1 (.D(data_in), .en(demultiplexer_1_out1), .Q(t1_q), .clk(clock));  // open: clr
  Register #(.trigger("falling")) t2 (.D(data_in), .en(demultiplexer_1_out3), .Q(t2_q), .clk(clock));  // open: clr
  Register #(.trigger("falling")) t3 (.D(data_in), .en(demultiplexer_1_out2), .Q(t3_q), .clk(clock));  // open: clr
  Register #(.trigger("falling")) t4 (.D(data_in), .en(demultiplexer_1_out4), .Q(t4_q), .clk(clock));  // open: clr
  Register #(.trigger("falling")) ZERO (
    .D({8{1'b0}}), .en(demultiplexer_1_out14), .Q(ZERO_q), .clk(clock));  // open: clr
  Register #(.trigger("falling")) SP (.D(data_in), .en(demultiplexer_1_out10), .Q(SP_q), .clk(clock));  // open: clr
  Multiplexer #(.select(4), .width(8), .enable("false")) multiplexer_1 (
    .in0(t0_q), .in1(t1_q), .in2(t2_q), .in3(t3_q), .in4(t4_q), .in15(ZERO_q), .out(data_out_A),
    .sel(addressA));  // open: in5, in6, in7, in8, in9, in10, in11, in12, in13, in14
  Multiplexer #(.select(4), .width(8)) multiplexer_2 (
    .in0(t0_q), .in1(t1_q), .in2(t2_q), .in3(t3_q), .in4(t4_q), .in10(SP_q), .in15(ZERO_q), .out(data_out_B),
    .sel(addressB__ReadOnly));  // open: in5, in6, in7, in8, in9, in11, in12, in13, in14, en
endmodule

module Control (
  input  [3:0] in_1,
  output bneq,
  output Shift,
  output RegDest,
  output Jump,
  output Branch,
  output MemRead,
  output MemToReg,
  output MemWrite,
  output ALUSrc,
  output RegWrite
);

  ROM #(.addrWidth(4), .dataWidth(10)) rom_1 (
    .addr(in_1), .data({bneq, Shift, RegDest, Jump, Branch, MemRead, MemToReg, MemWrite, ALUSrc, RegWrite}));  // open: sel

  // Notes on the sheet:
  //   contents of rom_1 (hex, n*v repeats v):
  //   40 20 3 3 81 81 1b 6 3 181 181 220 81 81 81 3
endmodule

module Instruction_Decode (
  input  [19:0] in_1,
  output [3:0] shiftAmount,
  output [3:0] DstReg,
  output [7:0] Address_Imm,
  output [3:0] SrcReg2,
  output [3:0] SrcReg1,
  output [7:0] TargetJump,
  output [3:0] opCode
);


  assign Address_Imm = in_1[7:0];
  assign DstReg = in_1[7:4];
  assign opCode = in_1[19:16];
  assign shiftAmount = in_1[3:0];
  assign SrcReg1 = in_1[15:12];
  assign SrcReg2 = in_1[11:8];
  assign TargetJump = in_1[15:8];
endmodule
