// Logisim project main.circ as structural Verilog: 3 circuits, main circuit main
module main (
  input  [19:0] input_code
);

  RAM #(.addrWidth(3)) ram_1 ();  // open: addr, data, sel, clk, ld, clr
  ROM #(.dataWidth(5)) rom_1 ();  // open: addr, data, sel
  // MIPS_ALU mips_alu_1: pin names not known
  Registers registers_1 ();  // open: data_in, in_2, out_3
endmodule

module ALU (
  input  [7:0] in_1,
  input  [7:0] in_2,
  input  [2:0] in_3,
  output [7:0] out_4
);

  wire [7:0] adder_1_out, and_1_out, nor_1_out, or_1_out, subtractor_1_out;

  Adder adder_1 (.a(in_1), .b(in_2), .out(adder_1_out));  // open: cin, cout
  Subtractor subtractor_1 (.a(in_1), .b(in_2), .out(subtractor_1_out));  // open: bin, bout
  assign and_1_out = in_1 & in_2;  // AND_Gate and_1, 8 bits wide
  assign or_1_out = in_1 | in_2;  // OR_Gate or_1, 8 bits wide
  assign nor_1_out = ~(in_1 | in_2);  // NOR_Gate nor_1, 8 bits wide
  Multiplexer #(.select(3), .width(8)) multiplexer_1 (
    .in0(adder_1_out), .in1(subtractor_1_out), .in2(and_1_out), .in3(or_1_out), .in4(nor_1_out), .out(out_4),
    .sel(in_3));  // open: in5, in6, in7, en
endmodule

module Registers (
  input  [3:0] data_in,
  input  [2:0] in_2,
  output [3:0] out_3
);

  wire demultiplexer_2_out0, demultiplexer_2_out1, demultiplexer_2_out2, demultiplexer_2_out3,
       demultiplexer_2_out4, demultiplexer_2_out7, undriven;
  wire [2:0] undriven_2;
  wire [3:0] demultiplexer_1_out0, demultiplexer_1_out1, demultiplexer_1_out2, demultiplexer_1_out3,
       demultiplexer_1_out4, demultiplexer_1_out7, t0_q, t1_q, t2_q, t3_q, t4_q, ZERO_q;

  Demultiplexer #(.select(3), .width(4)) demultiplexer_1 (
    .out0(demultiplexer_1_out0), .out1(demultiplexer_1_out1), .out2(demultiplexer_1_out2),
    .out3(demultiplexer_1_out3), .out4(demultiplexer_1_out4), .out7(demultiplexer_1_out7), .in(data_in),
    .sel(in_2));  // open: out5, out6, en
  Demultiplexer #(.select(3)) demultiplexer_2 (
    .out0(demultiplexer_2_out0), .out1(demultiplexer_2_out1), .out2(demultiplexer_2_out2),
    .out3(demultiplexer_2_out3), .out4(demultiplexer_2_out4), .out7(demultiplexer_2_out7), .in(1'b1),
    .sel(in_2));  // open: out5, out6, en
  Register #(.width(4)) t0 (
    .D(demultiplexer_1_out0), .en(demultiplexer_2_out0), .Q(t0_q), .clk(undriven));  // open: clr
  Register #(.width(4)) t1 (
    .D(demultiplexer_1_out1), .en(demultiplexer_2_out1), .Q(t1_q), .clk(undriven));  // open: clr
  Register #(.width(4)) t2 (
    .D(demultiplexer_1_out2), .en(demultiplexer_2_out2), .Q(t2_q), .clk(undriven));  // open: clr
  Register #(.width(4)) t3 (
    .D(demultiplexer_1_out3), .en(demultiplexer_2_out3), .Q(t3_q), .clk(undriven));  // open: clr
  Register #(.width(4)) t4 (
    .D(demultiplexer_1_out4), .en(demultiplexer_2_out4), .Q(t4_q), .clk(undriven));  // open: clr
  Register #(.width(4)) ZERO (
    .D(demultiplexer_1_out7), .en(demultiplexer_2_out7), .Q(ZERO_q), .clk(undriven));  // open: clr
  Multiplexer #(.select(3), .width(4)) multiplexer_1 (
    .in0(t0_q), .in1(t1_q), .in2(t2_q), .in3(t3_q), .in4(t4_q), .in5(ZERO_q), .out(out_3), .sel(undriven_2));  // open: in6, in7, en
endmodule
